# Fritzing sketch tccfri (saved by Fritzing 0.9.3b)
breadboards: 2

parts:
  Componente1 = RFID USB Reader
  Componente2 = Arduino Pro Mini (5V)
  Componente3 = Arduino Uno (Rev3)
  Componente4 = RFID USB Reader

nets:
  N1: Componente1.GNDT, Componente2.D3
  N2: Componente1.CP, Componente2.D9
  N3: Componente1.ANT2, Componente2.D4
  N4: Componente1.ANT1, Componente2.D8
  N5: Componente1.TX-O, Componente2.GND
  N6: Componente1.GND, Componente2.D2
  VCC: Componente1.VCC, Componente2.VCC
  N7: Componente3.D9_PWM, Componente4.GND
  N8: Componente3.D10_PWM/SS, Componente4.GNDT
  N9: Componente3.D11_PWM/MOSI, Componente4.ANT2
  N10: Componente3.D12/MISO, Componente4.ANT1
  3V3: Componente3.3V3, Componente4.VCC
  N11: Componente3.GND, Componente4.TX-O
